# Fritzing sketch listenup (saved by Fritzing 0.9.3b)

parts:
  SparkFun_RedBoard_Turbo1 = SparkFun RedBoard Turbo [part_number=14812]
  LCD1 = LCD screen  # not connected
  Part1 = Serial Enabled LCD Backpack [part_number=LCD-00258]
  NC-Button = Round Pushbutton

nets:
  N1: SparkFun_RedBoard_Turbo1.D1/TXO, Part1.RX
  N2: SparkFun_RedBoard_Turbo1.D2, NC-Button.leg1
  GND: SparkFun_RedBoard_Turbo1.GND, Part1.GND, NC-Button.leg0
  VIN: SparkFun_RedBoard_Turbo1.VIN, Part1.5V

custom parts:
  SparkFun RedBoard Turbo: If you’re ready to step up your Arduino game from older 8-bit/16MHz microcontrollers, the SparkFun RedBoard Turbo is a formidable alternative. At its heart, the RedBoard Turbo uses the ATSAMD21G18, which is an ARM Cortex M0+, 32-bit microcontroller that can run at up to 48MHz. With an impressive 4MB of external flash memory and a UF2 (USB Flashing Format) bootloader, the RedBoard Turbo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
  Serial Enabled LCD Backpack: The serial enabled LCD backpack allows you to control a parallel based LCD over a single-wire serial interface. The SerLCD backpack takes care of all the HD44780 commands allowing seamless integration with any micro that can communicate over a wide range of TTL serial baud rates. The SerLCD currently supports 16 and 20 character wide screens with 2 or 4 lines of display. Communication with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
